# Fritzing sketch IoToilet (saved by Fritzing 0.9.3b)
breadboards: 1

parts:
  LM1 = LM393 [chip_label=?]
  U2 = POT [package=alps_pot]
  R1 = Photocell (LDR) [package=THT]
  R2 = Resistor [tolerance=±10% resistance=10k package="0402 [SMD]"]
  R3 = Resistor [tolerance=±10% resistance=220 package="0402 [SMD]"]
  LED1 = LED - 3mm [color="Red (633nm)" package="3 mm [THT]"]
  S1 = Pushbutton [package="[THT]"]
  Part1 = Breadboard Power Supply Board SMD
  U1 = ESP-12F (ESP8266 WiFi Module) [part_number=ESP8266]

nets:
  N1: LM1.Output_1, LED1.cathode, U1.GPIO14
  N2: LM1.In_1_-, R1.pin_0, R2.Pin_0
  N3: LM1.In_1_+, U2.S
  VCC: LM1.VCC, U2.A, R1.pin_1, R3.Pin_0, Part1.VCC, U1.VCC, U1.EN
  GND: LM1.GND, U2.E, R2.Pin_1, S1.Pin_3, S1.Pin_4, Part1.GND, U1.GND
  N4: R3.Pin_1, LED1.anode
  N5: S1.Pin_1, S1.Pin_2, U1.RST

custom parts:
  ESP-12F (ESP8266 WiFi Module): WiFi Module based on the ESP8266 with onboard PCB antenna and UART communications
